// Logisim project ALU.circ as structural Verilog: 1 circuit, main circuit main
module main (
  input  [15:0] x,
  input  zx,
  input  nx,
  input  [15:0] y,
  input  no,
  input  zy,
  input  f,
  input  ny,
  output [15:0] Out
);

  wire [15:0] adder_1_out, And16_out, multiplexer_1_out, multiplexer_2_out, multiplexer_3_out,
       multiplexer_4_out, multiplexer_5_out, not_1_out, not_2_out, not_3_out;

  Multiplexer #(.width(16), .enable("false")) multiplexer_1 (
    .in0(x), .in1({16{1'b0}}), .out(multiplexer_1_out), .sel(zx));
  assign not_1_out = ~multiplexer_1_out;  // NOT_Gate not_1, 16 bits wide
  Multiplexer #(.width(16), .enable("false")) multiplexer_2 (
    .in0(y), .in1({16{1'b0}}), .out(multiplexer_2_out), .sel(zy));
  assign not_2_out = ~multiplexer_2_out;  // NOT_Gate not_2, 16 bits wide
  Multiplexer #(.width(16), .enable("false")) multiplexer_3 (
    .in0(multiplexer_1_out), .in1(not_1_out), .out(multiplexer_3_out), .sel(nx));
  Multiplexer #(.width(16), .enable("false")) multiplexer_4 (
    .in0(multiplexer_2_out), .in1(not_2_out), .out(multiplexer_4_out), .sel(ny));
  Adder #(.width(16)) adder_1 (.a(multiplexer_3_out), .b(multiplexer_4_out), .out(adder_1_out));  // open: cin, cout
  assign And16_out = multiplexer_3_out & multiplexer_4_out;  // AND_Gate And16, 16 bits wide
  Multiplexer #(.width(16), .enable("false")) multiplexer_5 (
    .in0(And16_out), .in1(adder_1_out), .out(multiplexer_5_out), .sel(f));
  assign not_3_out = ~multiplexer_5_out;  // NOT_Gate not_3, 16 bits wide
  Multiplexer #(.width(16), .enable("false")) multiplexer_6 (
    .in0(multiplexer_5_out), .in1(not_3_out), .out(Out), .sel(no));
endmodule
