// Logisim project Circuitos3.circ as structural Verilog: 25 circuits, main circuit Not
module Not (
  input  Entrada,
  output Salida
);

  nand NAnd (Salida, Entrada, Entrada);

  // Notes on the sheet:
  //   Circuito Not
endmodule

module And (
  input  a,
  input  b,
  output Salida
);

  wire nand_1_out;

  nand nand_1 (nand_1_out, a, b);
  not not_1 (Salida, nand_1_out);

  // Notes on the sheet:
  //   Circuito And
endmodule

module Or (
  input  a,
  input  b,
  input  a_2,
  input  b_2,
  output Salida,
  output Salida_2
);

  wire And_out, not_1_out, not_2_out, not_3_out, not_4_out;

  not not_1 (not_1_out, a);
  not not_2 (not_2_out, b);
  not not_3 (not_3_out, a_2);
  not not_4 (not_4_out, b_2);
  nand NAnd (Salida, not_1_out, not_2_out);
  and And (And_out, not_3_out, not_4_out);
  not Not_5 (Salida_2, And_out);

  // Notes on the sheet:
  //   2 Forma 
  //   1 Forma 
  //   Circuito Or
endmodule

module XOr (
  input  a,
  input  b,
  output Salida
);

  wire And_2_out, And_out, not_1_out, not_2_out;

  not not_1 (not_1_out, a);
  not not_2 (not_2_out, b);
  and And (And_out, not_1_out, b);
  and And_2 (And_2_out, a, not_2_out);
  or Or (Salida, And_out, And_2_out);

  // Notes on the sheet:
  //   Circuito XOr
endmodule

// a
module Mux (
  input  a,
  input  b,
  input  Sel,
  input  b_2,
  input  Sel_2,
  input  a_2,
  output Salida,
  output Salida_2
);

  wire And_2_out, And_3_out, And_4_out, And_5_out, And_6_out, And_7_out, And_8_out, And_9_out, And_10_out,
       And_out, not_1_out, not_2_out, not_3_out, not_4_out, not_5_out, Or_2_out, Or_3_out;

  not not_1 (not_1_out, Sel_2);
  not not_2 (not_2_out, a);
  not not_3 (not_3_out, b);
  and And (And_out, not_2_out, b);
  and And_2 (And_2_out, a, not_3_out);
  not not_4 (not_4_out, Sel);
  and And_3 (And_3_out, a, b);
  not not_5 (not_5_out, Sel);
  and And_4 (And_4_out, a, b);
  and And_5 (And_5_out, b_2, Sel_2);
  and And_6 (And_6_out, a_2, not_1_out);
  and And_7 (And_7_out, And_out, Sel);
  and And_8 (And_8_out, And_2_out, not_4_out);
  and And_9 (And_9_out, And_3_out, not_5_out);
  and And_10 (And_10_out, And_4_out, Sel);
  or Or (Salida_2, And_5_out, And_6_out);
  or Or_2 (Or_2_out, And_7_out, And_8_out);
  or Or_3 (Or_3_out, And_9_out, And_10_out);
  or Or_4 (Salida, Or_2_out, Or_3_out);

  // Notes on the sheet:
  //   1 Forma 
  //   2 Forma 
  //   Circuito Mux
endmodule

module DMux (
  input  In,
  input  Sel,
  output Y0_a,
  output Y1_b
);

  wire not_1_out;

  not not_1 (not_1_out, Sel);
  and And (Y0_a, In, not_1_out);
  and And_2 (Y1_b, In, Sel);

  // Notes on the sheet:
  //   Circuito DMux
endmodule

module Not16 (
  input  [15:0] In,
  output [15:0] Out
);

  assign Out = ~In;  // NOT_Gate not_1, 16 bits wide

  // Notes on the sheet:
  //   Circuito Not16
endmodule

module And16 (
  input  [15:0] a,
  input  [15:0] b,
  output [15:0] Out
);

  assign Out = a & b;  // AND_Gate And16, 16 bits wide

  // Notes on the sheet:
  //   Circuito And16
endmodule

module Or16 (
  input  [15:0] a,
  input  [15:0] b,
  output [15:0] out
);

  assign out = a | b;  // OR_Gate Or16, 16 bits wide

  // Notes on the sheet:
  //   Circuito Or16
endmodule

module Mux16 (
  input  [15:0] a,
  input  [15:0] b,
  input  Sel,
  output [15:0] Out
);

  Multiplexer #(.width(16), .enable("false")) multiplexer_1 (.in0(a), .in1(b), .out(Out), .sel(Sel));

  // Notes on the sheet:
  //   Circuito Mux16
endmodule

module Or8Way (
  input  [7:0] In,
  input  _0,
  input  _1,
  input  _2,
  input  _3,
  input  _4,
  input  _5,
  input  _6,
  input  _7,
  output Out,
  output Out_2
);

  wire Or_2_out, Or_3_out, Or_4_out, Or_5_out, Or_6_out, Or_out;

  or Or (Or_out, _0, _1);
  or Or_2 (Or_2_out, _2, _3);
  or Or_3 (Or_3_out, _4, _5);
  or Or_4 (Or_4_out, _6, _7);
  or Or8 (Out, In[0], In[1], In[2], In[3], In[4], In[5], In[6], In[7]);
  or Or_5 (Or_5_out, Or_out, Or_2_out);
  or Or_6 (Or_6_out, Or_3_out, Or_4_out);
  or Or_7 (Out_2, Or_5_out, Or_6_out);

  // Notes on the sheet:
  //   1 Forma 
  //   2 Forma 
  //   Circuito Or8Way
endmodule

module Mux4Way16 (
  input  [15:0] a,
  input  [15:0] b,
  input  [15:0] c,
  input  [15:0] d,
  input  [1:0] Sel,
  output [15:0] Out
);

  wire [15:0] multiplexer_1_out, multiplexer_2_out;

  Multiplexer #(.width(16)) multiplexer_1 (.in0(a), .in1(b), .out(multiplexer_1_out), .sel(Sel[0]));  // open: en
  Multiplexer #(.width(16)) multiplexer_2 (.in0(c), .in1(d), .out(multiplexer_2_out), .sel(Sel[0]));  // open: en
  Multiplexer #(.width(16)) multiplexer_3 (
    .in0(multiplexer_1_out), .in1(multiplexer_2_out), .out(Out), .sel(Sel[1]));  // open: en

  // Notes on the sheet:
  //   Circuito Mux4Way16
endmodule

module Mux8Way16 (
  input  [15:0] a,
  input  [15:0] b,
  input  [15:0] c,
  input  [15:0] d,
  input  [15:0] e,
  input  [15:0] f,
  input  [15:0] g,
  input  [2:0] Sel,
  input  [15:0] h,
  output [15:0] out_10
);

  wire [15:0] multiplexer_1_out, multiplexer_2_out;

  Multiplexer #(.select(2), .width(16), .enable("false")) multiplexer_1 (
    .in0(a), .in1(b), .in2(c), .in3(d), .out(multiplexer_1_out), .sel(Sel[1:0]));
  Multiplexer #(.select(2), .width(16), .enable("false")) multiplexer_2 (
    .in0(e), .in1(f), .in2(g), .in3(h), .out(multiplexer_2_out), .sel(Sel[1:0]));
  Multiplexer #(.width(16), .enable("false")) multiplexer_3 (
    .in0(multiplexer_1_out), .in1(multiplexer_2_out), .out(out_10), .sel(Sel[2]));

  // Notes on the sheet:
  //   Circuito Mux8Way16
endmodule

module DMux4way (
  input  In,
  input  [1:0] Sel,
  output a,
  output b,
  output c,
  output d
);

  wire demultiplexer_1_out0, demultiplexer_1_out1;

  Demultiplexer demultiplexer_1 (
    .out0(demultiplexer_1_out0), .out1(demultiplexer_1_out1), .in(In), .sel(Sel[1]));  // open: en
  Demultiplexer demultiplexer_2 (.out0(a), .out1(b), .in(demultiplexer_1_out0), .sel(Sel[0]));  // open: en
  Demultiplexer demultiplexer_3 (.out0(c), .out1(d), .in(demultiplexer_1_out1), .sel(Sel[0]));  // open: en

  // Notes on the sheet:
  //   Circuito DMux4Way
endmodule

module DMux8way (
  input  a,
  input  b,
  input  c,
  input  d,
  input  In,
  input  e,
  input  f,
  input  g,
  input  h,
  input  [2:0] Sel
);

  wire demultiplexer_1_out0, demultiplexer_1_out1, demultiplexer_2_out0, demultiplexer_2_out1,
       demultiplexer_3_out0, demultiplexer_3_out1, demultiplexer_4_out0, demultiplexer_4_out1,
       demultiplexer_5_out0, demultiplexer_5_out1, demultiplexer_6_out0, demultiplexer_6_out1,
       demultiplexer_7_out0, demultiplexer_7_out1;

  Demultiplexer demultiplexer_1 (
    .out0(demultiplexer_1_out0), .out1(demultiplexer_1_out1), .in(In), .sel(Sel[2]));  // open: en
  Demultiplexer demultiplexer_2 (
    .out0(demultiplexer_2_out0), .out1(demultiplexer_2_out1), .in(demultiplexer_1_out0), .sel(Sel[1]));  // open: en
  Demultiplexer demultiplexer_3 (
    .out0(demultiplexer_3_out0), .out1(demultiplexer_3_out1), .in(demultiplexer_1_out1), .sel(Sel[1]));  // open: en
  Demultiplexer demultiplexer_4 (
    .out0(demultiplexer_4_out0), .out1(demultiplexer_4_out1), .in(demultiplexer_2_out0), .sel(Sel[0]));  // open: en
  Demultiplexer demultiplexer_5 (
    .out0(demultiplexer_5_out0), .out1(demultiplexer_5_out1), .in(demultiplexer_2_out1), .sel(Sel[0]));  // open: en
  Demultiplexer demultiplexer_6 (
    .out0(demultiplexer_6_out0), .out1(demultiplexer_6_out1), .in(demultiplexer_3_out0), .sel(Sel[0]));  // open: en
  Demultiplexer demultiplexer_7 (
    .out0(demultiplexer_7_out0), .out1(demultiplexer_7_out1), .in(demultiplexer_3_out1), .sel(Sel[0]));  // open: en

  // Notes on the sheet:
  //   Circuito DMux8Way
endmodule

module FullAdder (
  input  a,
  input  b,
  input  c,
  output Carry,
  output Sum
);

  wire and_1_out, and_2_out, and_3_out, and_4_out, and_5_out, and_6_out, and_7_out, not_1_out, not_2_out,
       not_3_out, not_4_out, not_5_out, not_6_out, not_7_out, not_8_out, not_9_out;

  not not_1 (not_1_out, a);
  and and_1 (and_1_out, not_1_out, b, c);
  not not_2 (not_2_out, c);
  and and_2 (and_2_out, a, b, not_2_out);
  ExactlyOne xor_1 (.out(Carry), .in0(and_1_out), .in1(and_2_out), .in2(and_3_out), .in3(and_4_out));
  not not_3 (not_3_out, b);
  not not_4 (not_4_out, a);
  and and_3 (and_3_out, a, not_3_out, c);
  not not_5 (not_5_out, a);
  not not_6 (not_6_out, b);
  and and_4 (and_4_out, not_4_out, not_6_out, c);
  and and_5 (and_5_out, not_5_out, b, not_7_out);
  not not_7 (not_7_out, c);
  and and_6 (and_6_out, a, b, c);
  ExactlyOne xor_2 (.out(Sum), .in0(and_4_out), .in1(and_5_out), .in2(and_6_out), .in3(and_7_out));
  not not_8 (not_8_out, b);
  not not_9 (not_9_out, c);
  and and_7 (and_7_out, a, not_8_out, not_9_out);

  // Notes on the sheet:
  //   Circuito FullAdder
endmodule

module HalfAdder (
  input  a,
  input  b,
  output Sum,
  output Carry
);

  and And (Carry, a, b);
  xor XOr (Sum, a, b);

  // Notes on the sheet:
  //   Circuito HalfAdder
endmodule

module FullAdderResumido (
  input  a,
  input  b,
  input  Cin,
  output Sum,
  output CarryOut
);

  wire And_2_out, And_out, XOr_out;

  xor XOr (XOr_out, a, b);
  and And (And_out, a, b);
  and And_2 (And_2_out, XOr_out, Cin);
  xor XOr_2 (Sum, XOr_out, Cin);
  or Or (CarryOut, And_out, And_2_out);

  // Notes on the sheet:
  //   Circuito FullAdder Resumido
endmodule

module Add16 (
  input  a,
  input  b,
  input  a_2,
  input  b_2,
  input  a_3,
  input  b_3,
  input  a_4,
  input  b_4,
  input  a_5,
  input  b_5,
  input  a_6,
  input  b_6,
  input  a_7,
  input  b_7,
  input  a_8,
  input  b_8,
  input  a_9,
  input  b_9,
  input  a_10,
  input  b_10,
  input  a_11,
  input  b_11,
  input  a_12,
  input  b_12,
  input  a_13,
  input  b_13,
  input  a_14,
  input  b_14,
  input  a_15,
  input  b_15,
  input  a_16,
  input  b_16,
  output Sum,
  output Sum_2,
  output Sum_3,
  output Sum_4,
  output Sum_5,
  output Sum_6,
  output Sum_7,
  output Sum_8,
  output Sum_9,
  output Sum_10,
  output Sum_11,
  output Sum_12,
  output Sum_13,
  output Sum_14,
  output Sum_15,
  output Sum_16
);

  wire and_1_out, and_2_out, and_3_out, and_4_out, and_5_out, and_6_out, and_7_out, and_8_out, and_9_out,
       and_10_out, and_11_out, and_12_out, and_13_out, and_14_out, and_15_out, and_16_out, and_17_out,
       and_18_out, and_19_out, and_20_out, and_21_out, and_22_out, and_23_out, and_24_out, and_25_out,
       and_26_out, and_27_out, and_28_out, and_29_out, and_30_out, and_31_out, or_1_out, or_2_out, or_3_out,
       or_4_out, or_5_out, or_6_out, or_7_out, or_8_out, or_9_out, or_10_out, or_11_out, or_12_out,
       or_13_out, or_14_out, xor_2_out, xor_4_out, xor_6_out, xor_8_out, xor_10_out, xor_12_out, xor_14_out,
       xor_16_out, xor_18_out, xor_20_out, xor_22_out, xor_24_out, xor_26_out, xor_28_out, xor_30_out;

  xor xor_1 (Sum, a, b);
  and and_1 (and_1_out, a, b);
  xor xor_2 (xor_2_out, a_2, b_2);
  and and_2 (and_2_out, a_2, b_2);
  and and_3 (and_3_out, xor_2_out, and_1_out);
  xor xor_3 (Sum_2, xor_2_out, and_1_out);
  or or_1 (or_1_out, and_2_out, and_3_out);
  and and_4 (and_4_out, a_3, b_3);
  xor xor_4 (xor_4_out, a_3, b_3);
  and and_5 (and_5_out, xor_4_out, or_1_out);
  xor xor_5 (Sum_3, xor_4_out, or_1_out);
  or or_2 (or_2_out, and_4_out, and_5_out);
  and and_6 (and_6_out, a_4, b_4);
  xor xor_6 (xor_6_out, a_4, b_4);
  and and_7 (and_7_out, xor_6_out, or_2_out);
  xor xor_7 (Sum_4, xor_6_out, or_2_out);
  or or_3 (or_3_out, and_6_out, and_7_out);
  xor xor_8 (xor_8_out, a_5, b_5);
  and and_8 (and_8_out, a_5, b_5);
  and and_9 (and_9_out, xor_8_out, or_3_out);
  xor xor_9 (Sum_5, xor_8_out, or_3_out);
  or or_4 (or_4_out, and_8_out, and_9_out);
  and and_10 (and_10_out, a_6, b_6);
  xor xor_10 (xor_10_out, a_6, b_6);
  and and_11 (and_11_out, xor_10_out, or_4_out);
  xor xor_11 (Sum_6, xor_10_out, or_4_out);
  or or_5 (or_5_out, and_10_out, and_11_out);
  xor xor_12 (xor_12_out, a_7, b_7);
  and and_12 (and_12_out, a_7, b_7);
  and and_13 (and_13_out, xor_12_out, or_5_out);
  xor xor_13 (Sum_7, xor_12_out, or_5_out);
  or or_6 (or_6_out, and_12_out, and_13_out);
  and and_14 (and_14_out, a_8, b_8);
  xor xor_14 (xor_14_out, a_8, b_8);
  and and_15 (and_15_out, xor_14_out, or_6_out);
  xor xor_15 (Sum_8, xor_14_out, or_6_out);
  or or_7 (or_7_out, and_14_out, and_15_out);
  xor xor_16 (xor_16_out, a_9, b_9);
  and and_16 (and_16_out, a_9, b_9);
  and and_17 (and_17_out, xor_16_out, or_7_out);
  xor xor_17 (Sum_9, xor_16_out, or_7_out);
  or or_8 (or_8_out, and_16_out, and_17_out);
  and and_18 (and_18_out, a_10, b_10);
  xor xor_18 (xor_18_out, a_10, b_10);
  and and_19 (and_19_out, xor_18_out, or_8_out);
  xor xor_19 (Sum_10, xor_18_out, or_8_out);
  or or_9 (or_9_out, and_18_out, and_19_out);
  xor xor_20 (xor_20_out, a_11, b_11);
  and and_20 (and_20_out, a_11, b_11);
  and and_21 (and_21_out, xor_20_out, or_9_out);
  xor xor_21 (Sum_11, xor_20_out, or_9_out);
  or or_10 (or_10_out, and_20_out, and_21_out);
  and and_22 (and_22_out, a_12, b_12);
  xor xor_22 (xor_22_out, a_12, b_12);
  and and_23 (and_23_out, xor_22_out, or_10_out);
  xor xor_23 (Sum_12, xor_22_out, or_10_out);
  or or_11 (or_11_out, and_22_out, and_23_out);
  xor xor_24 (xor_24_out, a_13, b_13);
  and and_24 (and_24_out, a_13, b_13);
  and and_25 (and_25_out, xor_24_out, or_11_out);
  xor xor_25 (Sum_13, xor_24_out, or_11_out);
  or or_12 (or_12_out, and_24_out, and_25_out);
  and and_26 (and_26_out, a_14, b_14);
  xor xor_26 (xor_26_out, a_14, b_14);
  and and_27 (and_27_out, xor_26_out, or_12_out);
  xor xor_27 (Sum_14, xor_26_out, or_12_out);
  or or_13 (or_13_out, and_26_out, and_27_out);
  xor xor_28 (xor_28_out, a_15, b_15);
  and and_28 (and_28_out, a_15, b_15);
  and and_29 (and_29_out, xor_28_out, or_13_out);
  xor xor_29 (Sum_15, xor_28_out, or_13_out);
  or or_14 (or_14_out, and_28_out, and_29_out);
  xor xor_30 (xor_30_out, a_16, b_16);
  and and_30 (and_30_out, a_16, b_16);
  and and_31 (and_31_out, xor_30_out, or_14_out);
  xor xor_31 (Sum_16, xor_30_out, or_14_out);
  // OR_Gate or_15 has open pins: in0=and_30_out, in1=and_31_out, out=open

  // Notes on the sheet:
  //   Circuito Add16
endmodule

module Inc16 (
  input  [15:0] i,
  output [15:0] Out
);

  Adder #(.width(16)) adder_1 (.a(i), .b(16'h1), .out(Out));  // open: cin, cout

  // Notes on the sheet:
  //   Circuito Inc16
endmodule

module Bit (
  input  in,
  input  Load,
  output Out
);

  wire clock_1_out, multiplexer_1_out;

  Multiplexer multiplexer_1 (.in0(Out), .in1(in), .out(multiplexer_1_out), .sel(Load));  // open: en
  Clock clock_1 (.out(clock_1_out));
  D_Flip_Flop d_ff_1 (.clk(clock_1_out), .D(multiplexer_1_out), .Q(Out));  // open: Qn, preset, en, reset
endmodule

module Registro (
  input  [15:0] In,
  input  Load,
  output [15:0] Out
);

  wire Clock;

  Clock u_Clock (.out(Clock));
  Bit bit_1 (.in(In[0]), .Load(Load), .Out(Out[0]));
  Bit bit_2 (.in(In[1]), .Load(Load), .Out(Out[1]));
  Bit bit_3 (.in(In[2]), .Load(Load), .Out(Out[2]));
  Bit bit_4 (.in(In[3]), .Load(Load), .Out(Out[3]));
  Bit bit_5 (.in(In[4]), .Load(Load), .Out(Out[4]));
  Bit bit_6 (.in(In[5]), .Load(Load), .Out(Out[5]));
  Bit bit_7 (.in(In[6]), .Load(Load), .Out(Out[6]));
  Bit bit_8 (.in(In[7]), .Load(Load), .Out(Out[7]));
  Bit bit_9 (.in(In[8]), .Load(Load), .Out(Out[8]));
  Bit bit_10 (.in(In[9]), .Load(Load), .Out(Out[9]));
  Bit bit_11 (.in(In[10]), .Load(Load), .Out(Out[10]));
  Bit bit_12 (.in(In[11]), .Load(Load), .Out(Out[11]));
  Bit bit_13 (.in(In[12]), .Load(Load), .Out(Out[12]));
  Bit bit_14 (.in(In[13]), .Load(Load), .Out(Out[13]));
  Bit bit_15 (.in(In[14]), .Load(Load), .Out(Out[14]));
  Bit bit_16 (.in(In[15]), .Load(Load), .Out(Out[15]));
endmodule

module RAM8 (
  input  [15:0] In,
  input  Load,
  input  [2:0] Address,
  output [15:0] Out
);

  wire Clock, demultiplexer_1_out0, demultiplexer_1_out1, demultiplexer_1_out2, demultiplexer_1_out3,
       demultiplexer_1_out4, demultiplexer_1_out5, demultiplexer_1_out6, demultiplexer_1_out7;
  wire [15:0] registro_1_out, registro_2_out, registro_3_out, registro_4_out, registro_5_out, registro_6_out,
       registro_7_out, registro_8_out;

  Clock u_Clock (.out(Clock));
  Demultiplexer #(.select(3), .enable("false")) demultiplexer_1 (
    .out0(demultiplexer_1_out0), .out1(demultiplexer_1_out1), .out2(demultiplexer_1_out2),
    .out3(demultiplexer_1_out3), .out4(demultiplexer_1_out4), .out5(demultiplexer_1_out5),
    .out6(demultiplexer_1_out6), .out7(demultiplexer_1_out7), .in(Load), .sel(Address));
  Registro registro_1 (.In(In), .Load(demultiplexer_1_out0), .Out(registro_1_out));
  Registro registro_2 (.In(In), .Load(demultiplexer_1_out1), .Out(registro_2_out));
  Registro registro_3 (.In(In), .Load(demultiplexer_1_out2), .Out(registro_3_out));
  Registro registro_4 (.In(In), .Load(demultiplexer_1_out3), .Out(registro_4_out));
  Registro registro_5 (.In(In), .Load(demultiplexer_1_out4), .Out(registro_5_out));
  Registro registro_6 (.In(In), .Load(demultiplexer_1_out5), .Out(registro_6_out));
  Registro registro_7 (.In(In), .Load(demultiplexer_1_out6), .Out(registro_7_out));
  Registro registro_8 (.In(In), .Load(demultiplexer_1_out7), .Out(registro_8_out));
  Multiplexer #(.select(3), .width(16), .enable("false")) multiplexer_1 (
    .in0(registro_1_out), .in1(registro_2_out), .in2(registro_3_out), .in3(registro_4_out),
    .in4(registro_5_out), .in5(registro_6_out), .in6(registro_7_out), .in7(registro_8_out), .out(Out),
    .sel(Address));
endmodule

module RAM64 (
  input  [15:0] In,
  input  Load,
  input  [5:0] Address,
  output [15:0] Out
);

  wire Clock, demultiplexer_1_out0, demultiplexer_1_out1, demultiplexer_1_out2, demultiplexer_1_out3,
       demultiplexer_1_out4, demultiplexer_1_out5, demultiplexer_1_out6, demultiplexer_1_out7;
  wire [15:0] ram8_1_out, ram8_2_out, ram8_3_out, ram8_4_out, ram8_5_out, ram8_6_out, ram8_7_out, ram8_8_out;

  Clock u_Clock (.out(Clock));
  Demultiplexer #(.select(3), .enable("false")) demultiplexer_1 (
    .out0(demultiplexer_1_out0), .out1(demultiplexer_1_out1), .out2(demultiplexer_1_out2),
    .out3(demultiplexer_1_out3), .out4(demultiplexer_1_out4), .out5(demultiplexer_1_out5),
    .out6(demultiplexer_1_out6), .out7(demultiplexer_1_out7), .in(Load), .sel(Address[5:3]));
  RAM8 ram8_1 (.In(In), .Load(demultiplexer_1_out0), .Address(Address[2:0]), .Out(ram8_1_out));
  RAM8 ram8_2 (.In(In), .Load(demultiplexer_1_out1), .Address(Address[2:0]), .Out(ram8_2_out));
  RAM8 ram8_3 (.In(In), .Load(demultiplexer_1_out2), .Address(Address[2:0]), .Out(ram8_3_out));
  RAM8 ram8_4 (.In(In), .Load(demultiplexer_1_out3), .Address(Address[2:0]), .Out(ram8_4_out));
  RAM8 ram8_5 (.In(In), .Load(demultiplexer_1_out4), .Address(Address[2:0]), .Out(ram8_5_out));
  RAM8 ram8_6 (.In(In), .Load(demultiplexer_1_out5), .Address(Address[2:0]), .Out(ram8_6_out));
  RAM8 ram8_7 (.In(In), .Load(demultiplexer_1_out6), .Address(Address[2:0]), .Out(ram8_7_out));
  RAM8 ram8_8 (.In(In), .Load(demultiplexer_1_out7), .Address(Address[2:0]), .Out(ram8_8_out));
  Multiplexer #(.select(3), .width(16), .enable("false")) multiplexer_1 (
    .in0(ram8_1_out), .in1(ram8_2_out), .in2(ram8_3_out), .in3(ram8_4_out), .in4(ram8_5_out),
    .in5(ram8_6_out), .in6(ram8_7_out), .in7(ram8_8_out), .out(Out), .sel(Address[5:3]));
endmodule

module RAM512 (
  input  [15:0] In,
  input  Load,
  input  [8:0] Address,
  output [15:0] Out
);

  wire Clock, demultiplexer_1_out0, demultiplexer_1_out1, demultiplexer_1_out2, demultiplexer_1_out3,
       demultiplexer_1_out4, demultiplexer_1_out5, demultiplexer_1_out6, demultiplexer_1_out7;
  wire [15:0] ram64_1_out, ram64_2_out, ram64_3_out, ram64_4_out, ram64_5_out, ram64_6_out, ram64_7_out,
       ram64_8_out;

  Clock u_Clock (.out(Clock));
  Demultiplexer #(.select(3), .enable("false")) demultiplexer_1 (
    .out0(demultiplexer_1_out0), .out1(demultiplexer_1_out1), .out2(demultiplexer_1_out2),
    .out3(demultiplexer_1_out3), .out4(demultiplexer_1_out4), .out5(demultiplexer_1_out5),
    .out6(demultiplexer_1_out6), .out7(demultiplexer_1_out7), .in(Load), .sel(Address[8:6]));
  RAM64 ram64_1 (.In(In), .Load(demultiplexer_1_out0), .Address(Address[5:0]), .Out(ram64_1_out));
  RAM64 ram64_2 (.In(In), .Load(demultiplexer_1_out1), .Address(Address[5:0]), .Out(ram64_2_out));
  RAM64 ram64_3 (.In(In), .Load(demultiplexer_1_out2), .Address(Address[5:0]), .Out(ram64_3_out));
  RAM64 ram64_4 (.In(In), .Load(demultiplexer_1_out3), .Address(Address[5:0]), .Out(ram64_4_out));
  RAM64 ram64_5 (.In(In), .Load(demultiplexer_1_out4), .Address(Address[5:0]), .Out(ram64_5_out));
  RAM64 ram64_6 (.In(In), .Load(demultiplexer_1_out5), .Address(Address[5:0]), .Out(ram64_6_out));
  RAM64 ram64_7 (.In(In), .Load(demultiplexer_1_out6), .Address(Address[5:0]), .Out(ram64_7_out));
  RAM64 ram64_8 (.In(In), .Load(demultiplexer_1_out7), .Address(Address[5:0]), .Out(ram64_8_out));
  Multiplexer #(.select(3), .width(16), .enable("false")) multiplexer_1 (
    .in0(ram64_1_out), .in1(ram64_2_out), .in2(ram64_3_out), .in3(ram64_4_out), .in4(ram64_5_out),
    .in5(ram64_6_out), .in6(ram64_7_out), .in7(ram64_8_out), .out(Out), .sel(Address[8:6]));
endmodule
